// Logisim project 16-bit microprocessor.circ as structural Verilog: 5 circuits, main circuit main
module main (
);

  wire and_1_out, clock_1_out, control_unit_1_alu_input_2_sel, control_unit_1_dmwe,
       control_unit_1_r_write_en, control_unit_1_rs_select, control_unit_1_write_data_sel;
  wire [2:0] multiplexer_5_out;
  wire [3:0] multiplexer_2_out, multiplexer_3_out;
  wire [6:0] rom_1_data;
  wire [15:0] adder_1_out, bit_extender_1_out, bit_extender_2_out, main_1_p4, main_1_p7, main_1_p8,
       multiplexer_1_out, multiplexer_4_out, n16_bit_alu_1_results, ram_1_data, register_1_q;
  wire [17:7] rom_1_data_2;

  Clock clock_1 (.out(clock_1_out));
  Register #(.width(16)) register_1 (.D(adder_1_out), .Q(register_1_q), .clk(clock_1_out));  // open: en, clr
  Multiplexer #(.width(16), .enable("false")) multiplexer_1 (
    .in0(16'h1), .in1(bit_extender_1_out), .out(multiplexer_1_out), .sel(and_1_out));
  assign bit_extender_1_out = {{9{rom_1_data[6]}}, rom_1_data};  // Bit_Extender bit_extender_1
  Adder #(.width(16)) adder_1 (.a(register_1_q), .b(multiplexer_1_out), .out(adder_1_out));  // open: cin, cout
  and and_1 (and_1_out, rom_1_data_2[17], n16_bit_alu_1_results[0]);
  ROM #(.addrWidth(16), .dataWidth(18)) rom_1 (.addr(register_1_q), .data({rom_1_data_2, rom_1_data}));  // open: sel
  Multiplexer #(.width(4), .enable("false")) multiplexer_2 (
    .in0(rom_1_data_2[14:11]), .in1(rom_1_data_2[10:7]), .out(multiplexer_2_out),
    .sel(control_unit_1_rs_select));
  Multiplexer #(.width(4), .enable("false")) multiplexer_3 (
    .in0(rom_1_data[6:3]), .in1(rom_1_data_2[14:11]), .out(multiplexer_3_out), .sel(rom_1_data_2[17]));
  Control_Unit control_unit_1 (
    .Op_1(rom_1_data_2[16]), .Op_2(rom_1_data_2[15]), .R_write_en(control_unit_1_r_write_en),
    .rs_select(control_unit_1_rs_select), .DMWE(control_unit_1_dmwe),
    .write_data_sel(control_unit_1_write_data_sel), .Alu_input_2_sel(control_unit_1_alu_input_2_sel));
  // Register_File_main main_1: pin names not known; wires that end beside it: rom_1_data_2[14:11], multiplexer_2_out, multiplexer_3_out, main_1_p4, control_unit_1_r_write_en, clock_1_out, main_1_p7, main_1_p8
  assign bit_extender_2_out = {{12{1'b0}}, rom_1_data[6:3]};  // Bit_Extender bit_extender_2
  Multiplexer #(.width(16), .enable("false")) multiplexer_4 (
    .in0(main_1_p8), .in1(bit_extender_2_out), .out(multiplexer_4_out), .sel(control_unit_1_alu_input_2_sel));
  Multiplexer #(.width(3), .enable("false")) multiplexer_5 (
    .in0(rom_1_data[2:0]), .in1(3'b110), .out(multiplexer_5_out), .sel(rom_1_data_2[17]));
  RAM #(.addrWidth(11), .dataWidth(16), .bus("separate")) ram_1 (
    .addr({rom_1_data_2[10:7], rom_1_data}), .din(main_1_p7), .data(ram_1_data), .str(control_unit_1_dmwe),
    .clk(clock_1_out));  // open: sel, ld, clr
  _16_bit_ALU u_16_bit_alu_1 (
    .results(n16_bit_alu_1_results), .B(multiplexer_4_out), .A(main_1_p7), .Operation(multiplexer_5_out));  // open: Carry_Out, in_4, out_7
  Multiplexer #(.width(16), .enable("false")) multiplexer_6 (
    .in0(ram_1_data), .in1(n16_bit_alu_1_results), .out(main_1_p4), .sel(control_unit_1_write_data_sel));

  // Notes on the sheet:
  //   contents of rom_1 (hex, n*v repeats v):
  //   8810 9032 9853 a030 a890 e017 1f84b 39e0 5b39 3123 3a8c 1ff8b 237fd 460a 1f297 18385 14002 11005
  //   data
  //   rd
  //   rs
  //   rt
  //   rs data
  //   rt data
endmodule

// ALU
module _16_bit_ALU (
  input  [15:0] B,
  input  [15:0] A,
  input  [2:0] Operation,
  input  in_4,
  output [15:0] results,
  output Carry_Out,
  output out_7
);

  wire comparator_1_eq, comparator_1_gt, comparator_1_lt;
  wire [15:0] adder_1_out, and_1_out, bit_extender_1_out, bit_extender_2_out, bit_extender_3_out, or_1_out,
       subtractor_1_out, xor_1_out;

  Subtractor #(.width(16)) subtractor_1 (.a(A), .b(B), .out(subtractor_1_out), .bin(in_4), .bout(out_7));
  Comparator #(.width(16)) comparator_1 (
    .a(A), .b(B), .gt(comparator_1_gt), .eq(comparator_1_eq), .lt(comparator_1_lt));
  assign and_1_out = A & B;  // AND_Gate and_1, 16 bits wide
  assign or_1_out = A | B;  // OR_Gate or_1, 16 bits wide
  assign xor_1_out = A ^ B;  // XOR_Gate xor_1, 16 bits wide
  Adder #(.width(16)) adder_1 (.a(A), .b(B), .out(adder_1_out), .cin(1'b0), .cout(Carry_Out));
  assign bit_extender_1_out = {{15{1'b0}}, comparator_1_gt};  // Bit_Extender bit_extender_1
  assign bit_extender_2_out = {{15{1'b0}}, comparator_1_eq};  // Bit_Extender bit_extender_2
  assign bit_extender_3_out = {{15{1'b0}}, comparator_1_lt};  // Bit_Extender bit_extender_3
  Multiplexer #(.select(3), .width(16)) multiplexer_1 (
    .in0(and_1_out), .in1(or_1_out), .in2(xor_1_out), .in3(adder_1_out), .in4(subtractor_1_out),
    .in5(bit_extender_1_out), .in6(bit_extender_2_out), .in7(bit_extender_3_out), .out(results),
    .sel(Operation));  // open: en

  // Notes on the sheet:
  //   Operations  
  //   AND
  //   000
  //   001
  //   OR
  //   XOR
  //   010
  //   ADD
  //   011
  //   SUB
  //   100
  //   SGT
  //   101
  //   SEQ
  //   110
  //   111
  //   SLT
endmodule

module Control_Unit (
  input  Op_1,
  input  Op_2,
  output R_write_en,
  output rs_select,
  output DMWE,
  output write_data_sel,
  output Alu_input_2_sel
);

  wire not_1_out, not_2_out;

  not not_1 (not_1_out, Op_1);
  not not_2 (not_2_out, Op_2);
  or or_1 (R_write_en, not_1_out, Op_2);
  and and_1 (DMWE, Op_1, not_2_out);
  or or_2 (write_data_sel, not_2_out, Op_1);
  and and_2 (Alu_input_2_sel, Op_1, Op_2);

  assign rs_select = R_write_en;
endmodule

module testing (
);

  wire and_1_out, clock_1_out, control_unit_1_alu_input_2_sel, control_unit_1_dmwe,
       control_unit_1_r_write_en, control_unit_1_rs_select, control_unit_1_write_data_sel;
  wire [2:0] multiplexer_6_out;
  wire [3:0] multiplexer_2_out, multiplexer_3_out, multiplexer_4_out;
  wire [6:0] bit_extender_1_out;
  wire [15:0] adder_1_out, bit_extender_2_out, main_1_p4, main_1_p7, main_1_p8, multiplexer_1_out,
       multiplexer_5_out, n16_bit_alu_1_results, ram_1_data, register_1_q, undriven;
  wire [17:7] rom_1_data;

  Clock clock_1 (.out(clock_1_out));
  Register #(.width(16)) register_1 (.D(adder_1_out), .Q(register_1_q), .clk(clock_1_out));  // open: en, clr
  Bit_Extender #(.in_width(16), .out_width(7), .\type ("sign")) bit_extender_1 (
    .in(undriven), .out(bit_extender_1_out));
  Multiplexer #(.width(16), .enable("false")) multiplexer_1 (
    .in0(16'h1), .in1(undriven), .out(multiplexer_1_out), .sel(and_1_out));
  Adder #(.width(16)) adder_1 (.a(register_1_q), .b(multiplexer_1_out), .out(adder_1_out));  // open: cin, cout
  and and_1 (and_1_out, rom_1_data[17], n16_bit_alu_1_results[0]);
  ROM #(.addrWidth(16), .dataWidth(18)) rom_1 (
    .addr(register_1_q), .data({rom_1_data, bit_extender_1_out}));  // open: sel
  Multiplexer #(.width(4), .enable("false")) multiplexer_2 (
    .in0(rom_1_data[14:11]), .in1(rom_1_data[10:7]), .out(multiplexer_2_out), .sel(control_unit_1_rs_select));
  Multiplexer #(.width(4), .enable("false")) multiplexer_3 (
    .in0(multiplexer_2_out), .in1(rom_1_data[14:11]), .out(multiplexer_3_out), .sel(rom_1_data[17]));
  Multiplexer #(.width(4), .enable("false")) multiplexer_4 (
    .in0(bit_extender_1_out[6:3]), .in1(rom_1_data[10:7]), .out(multiplexer_4_out), .sel(rom_1_data[17]));
  Control_Unit control_unit_1 (
    .Op_1(rom_1_data[16]), .Op_2(rom_1_data[15]), .R_write_en(control_unit_1_r_write_en),
    .rs_select(control_unit_1_rs_select), .DMWE(control_unit_1_dmwe),
    .write_data_sel(control_unit_1_write_data_sel), .Alu_input_2_sel(control_unit_1_alu_input_2_sel));
  // Register_File_main main_1: pin names not known; wires that end beside it: rom_1_data[14:11], multiplexer_3_out, multiplexer_4_out, main_1_p4, control_unit_1_r_write_en, clock_1_out, main_1_p7, main_1_p8
  assign bit_extender_2_out = {{12{1'b0}}, bit_extender_1_out[6:3]};  // Bit_Extender bit_extender_2
  Multiplexer #(.width(16), .enable("false")) multiplexer_5 (
    .in0(main_1_p8), .in1(bit_extender_2_out), .out(multiplexer_5_out), .sel(control_unit_1_alu_input_2_sel));
  Multiplexer #(.width(3), .enable("false")) multiplexer_6 (
    .in0(bit_extender_1_out[2:0]), .in1(3'b110), .out(multiplexer_6_out), .sel(rom_1_data[17]));
  _16_bit_ALU u_16_bit_alu_1 (
    .results(n16_bit_alu_1_results), .B(multiplexer_5_out), .A(main_1_p7), .Operation(multiplexer_6_out));  // open: Carry_Out, in_4, out_7
  RAM #(.addrWidth(11), .dataWidth(16), .bus("separate")) ram_1 (
    .addr({rom_1_data[10:7], bit_extender_1_out}), .din(main_1_p7), .data(ram_1_data),
    .str(control_unit_1_dmwe), .clk(clock_1_out));  // open: sel, ld, clr
  Multiplexer #(.width(16), .enable("false")) multiplexer_7 (
    .in0(ram_1_data), .in1(n16_bit_alu_1_results), .out(main_1_p4), .sel(control_unit_1_write_data_sel));

  // Notes on the sheet:
  //   contents of rom_1 (hex, n*v repeats v):
  //   8810 9032 9853 a030 a890 3123 3a8c 433a 14002 13005 191e3
  //   rd
  //   rs
  //   rt
  //   data
  //   rs data
  //   rt data
endmodule

module backup (
);

  wire clock_1_out, control_unit_1_alu_input_2_sel, control_unit_1_dmwe, control_unit_1_r_write_en,
       control_unit_1_rs_select, control_unit_1_write_data_sel;
  wire [3:0] multiplexer_1_out;
  wire [15:0] adder_1_out, bit_extender_1_out, main_1_p4, main_1_p7, main_1_p8, multiplexer_2_out,
       n16_bit_alu_1_results, ram_1_data, register_1_q;
  wire [16:0] rom_1_data;

  Clock clock_1 (.out(clock_1_out));
  Register #(.width(16)) register_1 (.D(adder_1_out), .Q(register_1_q), .clk(clock_1_out));  // open: en, clr
  Adder #(.width(16)) adder_1 (.a(register_1_q), .b(16'h1), .out(adder_1_out));  // open: cin, cout
  ROM #(.addrWidth(16), .dataWidth(17)) rom_1 (.addr(register_1_q), .data(rom_1_data));  // open: sel
  Multiplexer #(.width(4), .enable("false")) multiplexer_1 (
    .in0(rom_1_data[14:11]), .in1(rom_1_data[10:7]), .out(multiplexer_1_out), .sel(control_unit_1_rs_select));
  Control_Unit control_unit_1 (
    .Op_1(rom_1_data[16]), .Op_2(rom_1_data[15]), .R_write_en(control_unit_1_r_write_en),
    .rs_select(control_unit_1_rs_select), .DMWE(control_unit_1_dmwe),
    .write_data_sel(control_unit_1_write_data_sel), .Alu_input_2_sel(control_unit_1_alu_input_2_sel));
  // Register_File_main main_1: pin names not known; wires that end beside it: rom_1_data[14:11], multiplexer_1_out, rom_1_data[6:3], main_1_p4, control_unit_1_r_write_en, clock_1_out, main_1_p7, main_1_p8
  assign bit_extender_1_out = {{12{1'b0}}, rom_1_data[6:3]};  // Bit_Extender bit_extender_1
  Multiplexer #(.width(16), .enable("false")) multiplexer_2 (
    .in0(main_1_p8), .in1(bit_extender_1_out), .out(multiplexer_2_out), .sel(control_unit_1_alu_input_2_sel));
  _16_bit_ALU u_16_bit_alu_1 (
    .results(n16_bit_alu_1_results), .B(multiplexer_2_out), .A(main_1_p7), .Operation(rom_1_data[2:0]));  // open: Carry_Out, in_4, out_7
  RAM #(.addrWidth(11), .dataWidth(16), .bus("separate")) ram_1 (
    .addr(rom_1_data[10:0]), .din(main_1_p7), .data(ram_1_data), .str(control_unit_1_dmwe), .clk(clock_1_out));  // open: sel, ld, clr
  Multiplexer #(.width(16), .enable("false")) multiplexer_3 (
    .in0(ram_1_data), .in1(n16_bit_alu_1_results), .out(main_1_p4), .sel(control_unit_1_write_data_sel));

  // Notes on the sheet:
  //   contents of rom_1 (hex, n*v repeats v):
  //   8810 9032 9853 a030 a890 3123 3a8c 433a 14002 13005 191e3
  //   rd
  //   rs
  //   rt
  //   data
  //   rs data
  //   rt data
endmodule
