// Logisim project projecgt.circ as structural Verilog: 9 circuits, main circuit main
// 2
module main (
  input  in_1,
  output CF,
  output OF,
  output ZF
);

  wire clock_1_out, clock_2_out, clock_3_out, control_unit_1_alu_2_imm, control_unit_1_alu_2_src,
       control_unit_1_en_jump, control_unit_1_mem_read, control_unit_1_mem_write, control_unit_1_rd_src_reg,
       control_unit_1_reg_write;
  wire [1:0] control_unit_1_wd_src;
  wire [2:0] control_unit_1_alu_sel;
  wire [3:0] multiplexer_2_out;
  wire [11:0] rom_1_data;
  wire [15:0] bit_extender_1_out, bit_extender_2_out, bit_extender_3_out, multiplexer_1_out,
       multiplexer_3_out, multiplexer_4_out, n16_bit_alu_1_result, n16_bit_register_file_1_readdata_1,
       n16_bit_register_file_1_readdata_2, pc_1_output, ram_1_data;
  wire [15:12] rom_1_data_2;

  Clock clock_1 (.out(clock_1_out));
  PC pc_1 (
    .Clock(clock_1_out), .Clear(in_1), .Output(pc_1_output), .Immediate(bit_extender_1_out),
    .Enable_Immediate(control_unit_1_en_jump));
  assign bit_extender_1_out = {{4{1'b0}}, rom_1_data};  // Bit_Extender bit_extender_1
  ROM #(.addrWidth(16), .dataWidth(16)) rom_1 (.addr(pc_1_output), .data({rom_1_data_2, rom_1_data}));  // open: sel
  Multiplexer #(.select(2), .width(16), .enable("false")) multiplexer_1 (
    .in0(n16_bit_alu_1_result), .in1(ram_1_data), .in2(n16_bit_register_file_1_readdata_1),
    .out(multiplexer_1_out), .sel(control_unit_1_wd_src));  // open: in3
  Multiplexer #(.width(4), .enable("false")) multiplexer_2 (
    .in0(rom_1_data[7:4]), .in1(rom_1_data[11:8]), .out(multiplexer_2_out), .sel(control_unit_1_rd_src_reg));
  _16_bit_Register_File u_16_bit_register_file_1 (
    .WriteData(multiplexer_1_out), .ReadData_1(n16_bit_register_file_1_readdata_1),
    .ReadData_2(n16_bit_register_file_1_readdata_2), .WriteRegister(rom_1_data[11:8]),
    .ReadRegister_1(multiplexer_2_out), .ReadRegister_2(rom_1_data[3:0]),
    .WriteEnable(control_unit_1_reg_write), .Clock(clock_2_out));
  Clock clock_2 (.out(clock_2_out));
  assign bit_extender_2_out = {{12{1'b0}}, rom_1_data[3:0]};  // Bit_Extender bit_extender_2
  Control_Unit control_unit_1 (
    .Rd_src_reg(control_unit_1_rd_src_reg), .Reg_write(control_unit_1_reg_write),
    .Mem_write(control_unit_1_mem_write), .Mem_read(control_unit_1_mem_read),
    .EN_Jump(control_unit_1_en_jump), .ALU_2_src(control_unit_1_alu_2_src),
    .ALU_2_imm(control_unit_1_alu_2_imm), .OPCODE(rom_1_data_2), .WD_src(control_unit_1_wd_src),
    .ALU_sel(control_unit_1_alu_sel));
  assign bit_extender_3_out = {{8{1'b0}}, rom_1_data[7:0]};  // Bit_Extender bit_extender_3
  Multiplexer #(.width(16), .enable("false")) multiplexer_3 (
    .in0(16'h1), .in1(bit_extender_2_out), .out(multiplexer_3_out), .sel(control_unit_1_alu_2_imm));
  Multiplexer #(.width(16), .enable("false")) multiplexer_4 (
    .in0(n16_bit_register_file_1_readdata_2), .in1(multiplexer_3_out), .out(multiplexer_4_out),
    .sel(control_unit_1_alu_2_src));
  Clock clock_3 (.out(clock_3_out));
  RAM #(.addrWidth(16), .dataWidth(16), .bus("separate")) ram_1 (
    .addr(bit_extender_3_out), .din(n16_bit_register_file_1_readdata_1), .data(ram_1_data),
    .str(control_unit_1_mem_write), .clk(clock_3_out), .ld(control_unit_1_mem_read));  // open: sel, clr
  _16_bit_ALU u_16_bit_alu_1 (
    .ALU_SEL(control_unit_1_alu_sel), .A(n16_bit_register_file_1_readdata_1), .B(multiplexer_4_out),
    .Result(n16_bit_alu_1_result), .Zero(ZF), .Overflow(OF), .Carry_Out(CF));

  // Notes on the sheet:
  //   Instructions Memory
  //   contents of rom_1 (hex, n*v repeats v):
  //   0 0 1 12 30 3
  //   12-BIT SPLITTER
  //   Rt
  //   Rd
  //   Rs
  //   OPCODE
  //   4-bit
  //   Immediate
  //   8-bit
  //   Immediate
endmodule

module _16_bit_Register_File (
  input  [3:0] ReadRegister_1,
  input  [3:0] ReadRegister_2,
  input  [3:0] WriteRegister,
  input  [15:0] WriteData,
  input  WriteEnable,
  input  Clock,
  output [15:0] ReadData_1,
  output [15:0] ReadData_2
);

  wire and_1_out, and_2_out, and_3_out, and_4_out, and_5_out, and_6_out, and_7_out, and_8_out, and_9_out,
       and_10_out, and_11_out, and_12_out, and_13_out, and_14_out, and_15_out, and_16_out, decoder_1_out0,
       decoder_1_out1, decoder_1_out2, decoder_1_out3, decoder_1_out4, decoder_1_out5, decoder_1_out6,
       decoder_1_out7, decoder_1_out8, decoder_1_out9, decoder_1_out10, decoder_1_out11, decoder_1_out12,
       decoder_1_out13, decoder_1_out14, decoder_1_out15;
  wire [15:0] register_1_q, register_2_q, register_3_q, register_4_q, register_5_q, register_6_q,
       register_7_q, register_8_q, register_9_q, register_10_q, register_11_q, register_12_q, register_13_q,
       register_14_q, register_15_q, register_16_q;

  Decoder #(.select(4), .enable("false")) decoder_1 (
    .out0(decoder_1_out0), .out1(decoder_1_out1), .out2(decoder_1_out2), .out3(decoder_1_out3),
    .out4(decoder_1_out4), .out5(decoder_1_out5), .out6(decoder_1_out6), .out7(decoder_1_out7),
    .out8(decoder_1_out8), .out9(decoder_1_out9), .out10(decoder_1_out10), .out11(decoder_1_out11),
    .out12(decoder_1_out12), .out13(decoder_1_out13), .out14(decoder_1_out14), .out15(decoder_1_out15),
    .sel(WriteRegister));
  and and_1 (and_1_out, decoder_1_out0, WriteEnable);
  and and_2 (and_2_out, decoder_1_out1, WriteEnable);
  and and_3 (and_3_out, decoder_1_out2, WriteEnable);
  and and_4 (and_4_out, decoder_1_out3, WriteEnable);
  and and_5 (and_5_out, decoder_1_out4, WriteEnable);
  and and_6 (and_6_out, decoder_1_out5, WriteEnable);
  and and_7 (and_7_out, decoder_1_out6, WriteEnable);
  and and_8 (and_8_out, decoder_1_out7, WriteEnable);
  and and_9 (and_9_out, decoder_1_out8, WriteEnable);
  and and_10 (and_10_out, decoder_1_out9, WriteEnable);
  and and_11 (and_11_out, decoder_1_out10, WriteEnable);
  and and_12 (and_12_out, decoder_1_out11, WriteEnable);
  and and_13 (and_13_out, decoder_1_out12, WriteEnable);
  and and_14 (and_14_out, decoder_1_out13, WriteEnable);
  and and_15 (and_15_out, decoder_1_out14, WriteEnable);
  and and_16 (and_16_out, decoder_1_out15, WriteEnable);
  Register #(.width(16)) register_1 (.D(WriteData), .en(and_1_out), .Q(register_1_q), .clk(Clock));  // open: clr
  Register #(.width(16)) register_2 (.D(WriteData), .en(and_2_out), .Q(register_2_q), .clk(Clock));  // open: clr
  Register #(.width(16)) register_3 (.D(WriteData), .en(and_3_out), .Q(register_3_q), .clk(Clock));  // open: clr
  Register #(.width(16)) register_4 (.D(WriteData), .en(and_4_out), .Q(register_4_q), .clk(Clock));  // open: clr
  Register #(.width(16)) register_5 (.D(WriteData), .en(and_5_out), .Q(register_5_q), .clk(Clock));  // open: clr
  Register #(.width(16)) register_6 (.D(WriteData), .en(and_6_out), .Q(register_6_q), .clk(Clock));  // open: clr
  Register #(.width(16)) register_7 (.D(WriteData), .en(and_7_out), .Q(register_7_q), .clk(Clock));  // open: clr
  Register #(.width(16)) register_8 (.D(WriteData), .en(and_8_out), .Q(register_8_q), .clk(Clock));  // open: clr
  Register #(.width(16)) register_9 (.D(WriteData), .en(and_9_out), .Q(register_9_q), .clk(Clock));  // open: clr
  Register #(.width(16)) register_10 (.D(WriteData), .en(and_10_out), .Q(register_10_q), .clk(Clock));  // open: clr
  Register #(.width(16)) register_11 (.D(WriteData), .en(and_11_out), .Q(register_11_q), .clk(Clock));  // open: clr
  Register #(.width(16)) register_12 (.D(WriteData), .en(and_12_out), .Q(register_12_q), .clk(Clock));  // open: clr
  Register #(.width(16)) register_13 (.D(WriteData), .en(and_13_out), .Q(register_13_q), .clk(Clock));  // open: clr
  Register #(.width(16)) register_14 (.D(WriteData), .en(and_14_out), .Q(register_14_q), .clk(Clock));  // open: clr
  Register #(.width(16)) register_15 (.D(WriteData), .en(and_15_out), .Q(register_15_q), .clk(Clock));  // open: clr
  Register #(.width(16)) register_16 (.D(WriteData), .en(and_16_out), .Q(register_16_q), .clk(Clock));  // open: clr
  Multiplexer #(.select(4), .width(16)) multiplexer_1 (
    .in0(register_1_q), .in1(register_2_q), .in2(register_3_q), .in3(register_4_q), .in4(register_5_q),
    .in5(register_6_q), .in6(register_7_q), .in7(register_8_q), .in8(register_9_q), .in9(register_10_q),
    .in10(register_11_q), .in11(register_12_q), .in12(register_13_q), .in13(register_14_q),
    .in14(register_15_q), .in15(register_16_q), .out(ReadData_1), .sel(ReadRegister_1));  // open: en
  Multiplexer #(.select(4), .width(16)) multiplexer_2 (
    .in0(register_1_q), .in1(register_2_q), .in2(register_3_q), .in3(register_4_q), .in4(register_5_q),
    .in5(register_6_q), .in6(register_7_q), .in7(register_8_q), .in8(register_9_q), .in9(register_10_q),
    .in10(register_11_q), .in11(register_12_q), .in12(register_13_q), .in13(register_14_q),
    .in14(register_15_q), .in15(register_16_q), .out(ReadData_2), .sel(ReadRegister_2));  // open: en
endmodule

// 16-bit\nALU
module _16_bit_ALU (
  input  [2:0] ALU_SEL,
  input  [15:0] A,
  input  [15:0] B,
  output [15:0] Result,
  output Zero,
  output Overflow,
  output Carry_Out
);

  wire n1_bit_alu_1_carry_out, n1_bit_alu_2_carry_out, n1_bit_alu_3_carry_out, n1_bit_alu_4_carry_out,
       n1_bit_alu_5_carry_out, n1_bit_alu_6_carry_out, n1_bit_alu_7_carry_out, n1_bit_alu_8_carry_out,
       n1_bit_alu_9_carry_out, n1_bit_alu_10_carry_out, n1_bit_alu_11_carry_out, n1_bit_alu_12_carry_out,
       n1_bit_alu_13_carry_out, n1_bit_alu_14_carry_out, n1_bit_alu_15_carry_out;

  _1_bit_ALU u_1_bit_alu_1 (
    .B(B[0]), .A(A[0]), .Carry_In(1'b0), .ALU_SEL(ALU_SEL), .result(Result[0]),
    .Carry_Out(n1_bit_alu_1_carry_out));
  _1_bit_ALU u_1_bit_alu_2 (
    .B(B[1]), .A(A[1]), .Carry_In(n1_bit_alu_1_carry_out), .ALU_SEL(ALU_SEL), .result(Result[1]),
    .Carry_Out(n1_bit_alu_2_carry_out));
  _1_bit_ALU u_1_bit_alu_3 (
    .B(B[2]), .A(A[2]), .Carry_In(n1_bit_alu_2_carry_out), .ALU_SEL(ALU_SEL), .result(Result[2]),
    .Carry_Out(n1_bit_alu_3_carry_out));
  _1_bit_ALU u_1_bit_alu_4 (
    .B(B[3]), .A(A[3]), .Carry_In(n1_bit_alu_3_carry_out), .ALU_SEL(ALU_SEL), .result(Result[3]),
    .Carry_Out(n1_bit_alu_4_carry_out));
  _1_bit_ALU u_1_bit_alu_5 (
    .B(B[4]), .A(A[4]), .Carry_In(n1_bit_alu_4_carry_out), .ALU_SEL(ALU_SEL), .result(Result[4]),
    .Carry_Out(n1_bit_alu_5_carry_out));
  _1_bit_ALU u_1_bit_alu_6 (
    .B(B[5]), .A(A[5]), .Carry_In(n1_bit_alu_5_carry_out), .ALU_SEL(ALU_SEL), .result(Result[5]),
    .Carry_Out(n1_bit_alu_6_carry_out));
  _1_bit_ALU u_1_bit_alu_7 (
    .B(B[6]), .A(A[6]), .Carry_In(n1_bit_alu_6_carry_out), .ALU_SEL(ALU_SEL), .result(Result[6]),
    .Carry_Out(n1_bit_alu_7_carry_out));
  _1_bit_ALU u_1_bit_alu_8 (
    .B(B[7]), .A(A[7]), .Carry_In(n1_bit_alu_7_carry_out), .ALU_SEL(ALU_SEL), .result(Result[7]),
    .Carry_Out(n1_bit_alu_8_carry_out));
  _1_bit_ALU u_1_bit_alu_9 (
    .B(B[8]), .A(A[8]), .Carry_In(n1_bit_alu_8_carry_out), .ALU_SEL(ALU_SEL), .result(Result[8]),
    .Carry_Out(n1_bit_alu_9_carry_out));
  _1_bit_ALU u_1_bit_alu_10 (
    .B(B[9]), .A(A[9]), .Carry_In(n1_bit_alu_9_carry_out), .ALU_SEL(ALU_SEL), .result(Result[9]),
    .Carry_Out(n1_bit_alu_10_carry_out));
  _1_bit_ALU u_1_bit_alu_11 (
    .B(B[10]), .A(A[10]), .Carry_In(n1_bit_alu_10_carry_out), .ALU_SEL(ALU_SEL), .result(Result[10]),
    .Carry_Out(n1_bit_alu_11_carry_out));
  _1_bit_ALU u_1_bit_alu_12 (
    .B(B[11]), .A(A[11]), .Carry_In(n1_bit_alu_11_carry_out), .ALU_SEL(ALU_SEL), .result(Result[11]),
    .Carry_Out(n1_bit_alu_12_carry_out));
  _1_bit_ALU u_1_bit_alu_13 (
    .B(B[12]), .A(A[12]), .Carry_In(n1_bit_alu_12_carry_out), .ALU_SEL(ALU_SEL), .result(Result[12]),
    .Carry_Out(n1_bit_alu_13_carry_out));
  _1_bit_ALU u_1_bit_alu_14 (
    .B(B[13]), .A(A[13]), .Carry_In(n1_bit_alu_13_carry_out), .ALU_SEL(ALU_SEL), .result(Result[13]),
    .Carry_Out(n1_bit_alu_14_carry_out));
  _1_bit_ALU u_1_bit_alu_15 (
    .B(B[14]), .A(A[14]), .Carry_In(n1_bit_alu_14_carry_out), .ALU_SEL(ALU_SEL), .result(Result[14]),
    .Carry_Out(n1_bit_alu_15_carry_out));
  _1_bit_ALU u_1_bit_alu_16 (
    .B(B[15]), .A(A[15]), .Carry_In(n1_bit_alu_15_carry_out), .ALU_SEL(ALU_SEL), .result(Result[15]),
    .Carry_Out(Carry_Out));
  xor xor_1 (Overflow, n1_bit_alu_15_carry_out, Carry_Out);
  nor nor_1 (Zero, Result[0], Result[1], Result[2], Result[3], Result[4], Result[5], Result[6], Result[7], Result[8], Result[9], Result[10], Result[11], Result[12], Result[13], Result[14], Result[15]);
endmodule

// 1-bit\nALU
module _1_bit_ALU (
  input  B,
  input  A,
  input  Carry_In,
  input  [2:0] ALU_SEL,
  output result,
  output Carry_Out
);

  wire adder_1_out, and_1_out, assert_subtract_1_out, multiplexer_1_out, not_1_out, not_2_out, or_1_out,
       or_2_out, xor_1_out;

  Assert_Subtract assert_subtract_1 (.Operation(ALU_SEL), .Out(assert_subtract_1_out));
  not not_1 (not_1_out, B);
  Multiplexer #(.enable("false")) multiplexer_1 (
    .in0(B), .in1(not_1_out), .out(multiplexer_1_out), .sel(assert_subtract_1_out));
  or or_1 (or_1_out, Carry_In, assert_subtract_1_out);
  Adder #(.width(1)) adder_1 (.a(A), .b(multiplexer_1_out), .out(adder_1_out), .cin(or_1_out), .cout(Carry_Out));
  and and_1 (and_1_out, A, B);
  or or_2 (or_2_out, A, B);
  xor xor_1 (xor_1_out, A, B);
  not not_2 (not_2_out, A);
  Multiplexer #(.select(3)) multiplexer_2 (
    .in0(adder_1_out), .in1(adder_1_out), .in2(and_1_out), .in3(or_2_out), .in4(xor_1_out), .in5(not_2_out),
    .out(result), .sel(ALU_SEL));  // open: in6, in7, en
endmodule

// Assert\nSUB
module Assert_Subtract (
  input  [2:0] Operation,
  output Out
);

  and and_1 (Out, ~Operation[2], ~Operation[1], Operation[0]);  // AND_Gate
endmodule

module PC (
  input  Enable_Immediate,
  input  [15:0] Immediate,
  input  Clock,
  input  Clear,
  output [15:0] Output
);

  wire not_1_out;
  wire [15:0] adder_1_out, controlled_buffer_1_out;

  assign controlled_buffer_1_out = Enable_Immediate ? Immediate : 16'bz;  // Controlled_Buffer controlled_buffer_1
  not not_1 (not_1_out, Enable_Immediate);
  assign controlled_buffer_1_out = not_1_out ? adder_1_out : 16'bz;  // Controlled_Buffer controlled_buffer_2
  Register #(.width(16)) PC_Register (.D(controlled_buffer_1_out), .Q(Output), .clk(Clock), .clr(Clear));  // open: en
  Adder #(.width(16)) adder_1 (.a(Output), .b(16'h1), .out(adder_1_out));  // open: cin, cout
endmodule

// CU
module Control_Unit (
  input  [3:0] OPCODE,
  output Rd_src_reg,
  output Reg_write,
  output Mem_write,
  output Mem_read,
  output [1:0] WD_src,
  output EN_Jump,
  output ALU_2_src,
  output ALU_2_imm,
  output [2:0] ALU_sel
);

  wire and_6_out, and_7_out, not_1_out, not_2_out, not_3_out, not_5_out, not_6_out, not_7_out, not_8_out;

  and and_1 (Rd_src_reg, OPCODE[3], OPCODE[1], OPCODE[0]);
  not not_1 (not_1_out, OPCODE[2]);
  not not_2 (not_2_out, OPCODE[1]);
  and and_2 (Mem_write, OPCODE[3], OPCODE[1], OPCODE[0]);
  not not_3 (not_3_out, OPCODE[0]);
  and and_3 (WD_src[1], OPCODE[3], OPCODE[2]);
  and and_4 (WD_src[0], OPCODE[3], OPCODE[1]);
  and and_5 (EN_Jump, OPCODE[3], OPCODE[2], OPCODE[0]);
  and and_6 (and_6_out, OPCODE[2], OPCODE[1]);
  not not_4 (ALU_2_imm, OPCODE[3]);
  not not_5 (not_5_out, OPCODE[1]);
  not not_6 (not_6_out, OPCODE[2]);
  not not_7 (not_7_out, OPCODE[3]);
  and and_7 (and_7_out, not_1_out, not_2_out);
  not not_8 (not_8_out, OPCODE[0]);
  and and_8 (Mem_read, OPCODE[3], OPCODE[1], not_3_out);
  or or_1 (ALU_2_src, and_6_out, OPCODE[3]);
  and and_9 (ALU_sel[2], OPCODE[2], not_5_out);
  and and_10 (ALU_sel[1], not_6_out, OPCODE[1]);
  or or_2 (Reg_write, not_7_out, and_7_out, not_8_out);

  assign ALU_sel[0] = OPCODE[0];
endmodule

module Old_Control_Unit (
  input  [3:0] Opcode,
  output [2:0] ALU_SEL,
  output Reg_write,
  output Mem_write,
  output Rd_src_reg,
  output Mem_read,
  output [1:0] WD_src,
  output EN_Jump,
  output ALU_2_src,
  output ALU_2_imm
);

  wire and_1_out, and_2_out, and_3_out;

  and ALU_SEL_2 (ALU_SEL[2], Opcode[2], ~Opcode[1]);  // AND_Gate
  and ALU_SEL_1 (ALU_SEL[1], ~Opcode[2], Opcode[1]);  // AND_Gate
  and and_1 (and_1_out, ~Opcode[2], ~Opcode[1]);  // AND_Gate
  and and_2 (and_2_out, ~Opcode[2], ~Opcode[0]);  // AND_Gate
  and and_3 (and_3_out, Opcode[2], Opcode[1]);
  and WD_src_1 (WD_src[1], Opcode[3], Opcode[2]);
  and WD_src_0 (WD_src[0], Opcode[3], Opcode[1]);
  or or_1 (Reg_write, ~Opcode[3], and_1_out, and_2_out);  // OR_Gate
  and and_4 (Mem_write, Opcode[3], Opcode[1], Opcode[0]);
  and and_5 (Mem_read, Opcode[3], Opcode[1], ~Opcode[0]);  // AND_Gate
  or or_2 (ALU_2_src, Opcode[3], and_3_out);
  not not_1 (ALU_2_imm, Opcode[3]);
  and and_6 (EN_Jump, Opcode[3], Opcode[2]);
  and and_7 (Rd_src_reg, Opcode[3], Opcode[1]);

  assign ALU_SEL[0] = Opcode[0];
endmodule

module test (
  input  in_1,
  output CF,
  output OF,
  output ZF
);

  wire clock_1_out, clock_2_out, control_unit_1_alu_2_imm, control_unit_1_alu_2_src, control_unit_1_en_jump,
       control_unit_1_mem_read, control_unit_1_mem_write, control_unit_1_rd_src_reg, control_unit_1_reg_write;
  wire [1:0] control_unit_1_wd_src;
  wire [2:0] control_unit_1_alu_sel;
  wire [3:0] multiplexer_2_out;
  wire [11:0] rom_1_data;
  wire [15:0] bit_extender_1_out, bit_extender_2_out, bit_extender_3_out, multiplexer_1_out,
       multiplexer_3_out, multiplexer_4_out, n16_bit_alu_1_result, n16_bit_register_file_1_readdata_1,
       n16_bit_register_file_1_readdata_2, pc_1_output, ram_1_data;
  wire [15:12] rom_1_data_2;

  Clock clock_1 (.out(clock_1_out));
  PC pc_1 (
    .Clock(clock_1_out), .Clear(in_1), .Output(pc_1_output), .Immediate(bit_extender_1_out),
    .Enable_Immediate(control_unit_1_en_jump));
  assign bit_extender_1_out = {{4{1'b0}}, rom_1_data};  // Bit_Extender bit_extender_1
  ROM #(.addrWidth(16), .dataWidth(16)) rom_1 (.addr(pc_1_output), .data({rom_1_data_2, rom_1_data}));  // open: sel
  Multiplexer #(.select(2), .width(16), .enable("false")) multiplexer_1 (
    .in0(n16_bit_alu_1_result), .in1(ram_1_data), .in2(n16_bit_register_file_1_readdata_1),
    .out(multiplexer_1_out), .sel(control_unit_1_wd_src));  // open: in3
  Multiplexer #(.width(4), .enable("false")) multiplexer_2 (
    .in0(rom_1_data[7:4]), .in1(rom_1_data[11:8]), .out(multiplexer_2_out), .sel(control_unit_1_rd_src_reg));
  _16_bit_Register_File u_16_bit_register_file_1 (
    .WriteData(multiplexer_1_out), .ReadData_1(n16_bit_register_file_1_readdata_1),
    .ReadData_2(n16_bit_register_file_1_readdata_2), .WriteRegister(rom_1_data[11:8]),
    .ReadRegister_1(multiplexer_2_out), .ReadRegister_2(rom_1_data[3:0]),
    .WriteEnable(control_unit_1_reg_write), .Clock(clock_2_out));
  Clock clock_2 (.out(clock_2_out));
  assign bit_extender_2_out = {{12{1'b0}}, rom_1_data[3:0]};  // Bit_Extender bit_extender_2
  Control_Unit control_unit_1 (
    .Rd_src_reg(control_unit_1_rd_src_reg), .Reg_write(control_unit_1_reg_write),
    .Mem_write(control_unit_1_mem_write), .Mem_read(control_unit_1_mem_read),
    .EN_Jump(control_unit_1_en_jump), .ALU_2_src(control_unit_1_alu_2_src),
    .ALU_2_imm(control_unit_1_alu_2_imm), .OPCODE(rom_1_data_2), .WD_src(control_unit_1_wd_src),
    .ALU_sel(control_unit_1_alu_sel));
  assign bit_extender_3_out = {{8{1'b0}}, rom_1_data[7:0]};  // Bit_Extender bit_extender_3
  Multiplexer #(.width(16), .enable("false")) multiplexer_3 (
    .in0(16'h1), .in1(bit_extender_2_out), .out(multiplexer_3_out), .sel(control_unit_1_alu_2_imm));
  Multiplexer #(.width(16), .enable("false")) multiplexer_4 (
    .in0(n16_bit_register_file_1_readdata_2), .in1(multiplexer_3_out), .out(multiplexer_4_out),
    .sel(control_unit_1_alu_2_src));
  RAM #(.addrWidth(16), .dataWidth(16), .bus("separate")) ram_1 (
    .addr(bit_extender_3_out), .din(n16_bit_register_file_1_readdata_1), .data(ram_1_data),
    .str(control_unit_1_mem_write), .ld(control_unit_1_mem_read));  // open: sel, clk, clr
  _16_bit_ALU u_16_bit_alu_1 (
    .ALU_SEL(control_unit_1_alu_sel), .A(n16_bit_register_file_1_readdata_1), .B(multiplexer_4_out),
    .Result(n16_bit_alu_1_result), .Zero(ZF), .Overflow(OF), .Carry_Out(CF));

  // Notes on the sheet:
  //   Instructions Memory
  //   contents of rom_1 (hex, n*v repeats v):
  //   0 a652 2222 3333 4444 5555 6666 7777 8888 9999 aaaa bbbb cccc
  //   12-BIT SPLITTER
  //   Rt
  //   Rd
  //   Rs
  //   OPCODE
  //   4-bit
  //   Immediate
  //   8-bit
  //   Immediate
endmodule
